# Fritzing sketch rgb_led (saved by Fritzing 0.9.2b)
breadboards: 1

parts:
  Part1 = Intel Galileo Gen2
  R1 = Resistor [tolerance=±5% resistance=220 package=THT]
  R2 = Resistor [tolerance=±5% resistance=220 package=THT]
  R3 = Resistor [tolerance=±5% resistance=220 package=THT]
  LED1 = RGB LED - (4 legs) [package="5 mm [THT]"]

nets:
  N1: Part1.D3_PWM, R3.Pin_1
  N2: Part1.D5_PWM, R2.Pin_1
  N3: Part1.D6_PWM, R1.Pin_1
  N4: Part1.3V3, LED1.green_cathode
  N5: R1.Pin_0, LED1.red_cathode
  N6: R2.Pin_0, LED1.common_anode
  N7: R3.Pin_0, LED1.blue_cathode
